# Fritzing sketch ControlCircuitBoard (saved by Fritzing 1.0.3b)

parts:
  Bauteil3 = INA219 High Side DC Current Sensor Breakout [part_number=904]
  Bauteil4 = INA219 High Side DC Current Sensor Breakout [part_number=904]
  Bauteil5 = Adafruit DC+Stepper FeatherWing [part_number="Adafruit #2927"]  # not connected
  Adafruit_Feather_nRF52 = Adafruit Feather nRF52 [part_number="Adafruit #3406"]
  U2 = Molex Picoblade Series Header [part_number=0533980471 package=Picoblade-53398-0471]
  U3 = Molex Picoblade Series Header [part_number=0533980471 package=Picoblade-53398-0471]  # not connected
  U4 = Molex Picoblade Series Header [part_number=0532610219 package=Picoblade-53261-0219]  # not connected

nets:
  VCC: Bauteil3.VCC, Bauteil4.VCC, Adafruit_Feather_nRF52.3.3V, U2.4
  GND: Bauteil3.GND, Bauteil4.GND, Adafruit_Feather_nRF52.GND, U2.3
  N1: Bauteil3.SCL, Bauteil4.SCL, Adafruit_Feather_nRF52.SCL
  N2: Bauteil3.SDA, Bauteil4.SDA, Adafruit_Feather_nRF52.SDA
  N3: Adafruit_Feather_nRF52.A1/0.03, U2.2
  N4: Adafruit_Feather_nRF52.A2/0.04, U2.1

custom parts:
  INA219 High Side DC Current Sensor Breakout: This breakout board will solve all your power-monitoring problems. Instead of struggling with two multimeters, you can just use the handy INA219B chip on this breakout to both measure both the high side voltage and DC current draw over I2C with 1% precision. Most current-measuring devices such as our current panel meter are only good for low side measuring. That means that unless you want to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
  Adafruit DC+Stepper FeatherWing: This is the DC Motor + Stepper FeatherWing which will let you use 2 x bi-polar stepper motors or 4 x brushed DC motorx (or 1 stepper and 2 DC motors). Using our Feather Stacking Headers or Feather Female Headers you can connect a FeatherWing on top or bottom of your Feather board and let the board take flight! The original Adafruit Motorshield Kit is one of our most beloved kits, which is why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
